# Fritzing sketch Untitled Sketch (saved by Fritzing 0.9.2b)
breadboards: 1

parts:
  Bauteil1 = Arduino Nano (Rev3.0)
  Bauteil2 = EasyDriver_v44
  M1 = Stepper Motor - Bipolar
  S1 = Pushbutton [package=THT]
  R1 = Resistor [tolerance=±5% resistance=1k package=THT]
  R2 = Resistor [tolerance=±5% resistance=1k package=THT]
  R3 = Resistor [tolerance=±5% resistance=1k package=THT]
  R4 = Resistor [tolerance=±5% resistance=1k package=THT]
  J2 = female pin header, 2 pins [form="♀ (female)"]
  J3 = female pin header, 4 pins [form="♀ (female)"]

nets:
  N1: Bauteil1.D6, S1.leg0, J2.pin2
  N2: Bauteil1.D7, S1.leg1, J2.pin1
  N3: Bauteil1.D9, R3.Pin_0, J3.pin4
  N4: Bauteil1.D10, R4.Pin_0, J3.pin3
  N5: Bauteil1.D11/MOSI, R1.Pin_0, J3.pin2
  N6: Bauteil1.D12/MISO, R2.Pin_0, J3.pin1
  N7: Bauteil2.OUT2A, M1.A
  N8: Bauteil2.OUT2B, M1.C
  N9: Bauteil2.OUT1A, M1.B
  N10: Bauteil2.OUT1B, M1.D
  N11: R1.Pin_1, R2.Pin_1, R3.Pin_1, R4.Pin_1
